// Logisim project ex2.circ as structural Verilog: 1 circuit, main circuit compute_BrUn
module compute_BrUn (
  input  [31:0] INSTRUCTION,
  output BrUn
);

  Comparator #(.mode("unsigned"), .width(3)) comparator_1 (
    .a(3'b101), .b(INSTRUCTION[14:12]), .lt(BrUn));  // open: gt, eq
endmodule
