// Logisim project control-logic.circ as structural Verilog: 1 circuit, main circuit control_logic
module control_logic (
  input  [31:0] Instruction,
  input  BrEq,
  input  BrLt,
  output PCSel,
  output RegWEn,
  output [2:0] ImmSel,
  output BrUn,
  output ASel,
  output BSel,
  output [3:0] ALUSel,
  output MemRW,
  output [1:0] WBSel
);

  wire and_34_out, and_35_out, and_36_out, and_37_out, and_38_out, and_39_out, B, f3_0, f3_1, f3_2, f3_3,
       f3_4, f3_5, f3_6, f3_7, f7_00, f7_01, f7_20, I1, I2, I3, is_add, is_addi, is_and, is_andi, is_auipc,
       is_beq, is_bge, is_bgeu, is_blt, is_bltu, is_bne, is_jal, is_jalr, is_lb, is_lh, is_lui, is_lw,
       is_mul, is_mulh, is_mulhu, is_or, is_ori, is_sb, is_sh, is_sll, is_slli, is_slt, is_slti, is_sra,
       is_srai, is_srl, is_srli, is_sub, is_sw, is_xor, is_xori, not_1_out, not_2_out, not_3_out, or_1_out,
       or_2_out, R, S;
  wire [5:0] priority_encoder_1_out;
  wire [15:14] rom_1_data;

  Priority_Encoder #(.select_enc(6)) priority_encoder_1 (
    .in0(is_add), .in1(is_mul), .in2(is_sub), .in3(is_sll), .in4(is_mulh), .in5(is_mulhu), .in6(is_slt),
    .in7(is_xor), .in8(is_srl), .in9(is_sra), .in10(is_or), .in11(is_and), .in12(is_lb), .in13(is_lh),
    .in14(is_lw), .in15(is_addi), .in16(is_slli), .in17(is_slti), .in18(is_xori), .in19(is_srli),
    .in20(is_srai), .in21(is_ori), .in22(is_andi), .in23(is_sb), .in24(is_sh), .in25(is_sw), .in26(is_beq),
    .in27(is_bne), .in28(is_blt), .in29(is_bge), .in30(is_bltu), .in31(is_bgeu), .in32(is_auipc),
    .in33(is_lui), .in34(is_jal), .in35(is_jalr), .out(priority_encoder_1_out));  // open: in36, in37, in38, in39, in40, in41, in42, in43, in44, in45, in46, in47, in48, in49, in50, in51, in52, in53, in54, in55, in56, in57, in58, in59, in60, in61, in62, in63, gs, en_out, en_in
  ROM #(.addrWidth(6), .dataWidth(16)) rom_1 (
    .addr(priority_encoder_1_out), .data({rom_1_data, WBSel, MemRW, ALUSel, BSel, ASel, BrUn, ImmSel, RegWEn}));
  Comparator #(.width(7)) comparator_1 (.a(Instruction[6:0]), .b(7'b0110011), .eq(R));  // open: gt, lt
  Comparator #(.width(7)) comparator_2 (.a(Instruction[6:0]), .b(7'b0000011), .eq(I1));  // open: gt, lt
  Comparator #(.width(7)) comparator_3 (.a(Instruction[6:0]), .b(7'b0010011), .eq(I2));  // open: gt, lt
  Comparator #(.width(7)) comparator_4 (.a(Instruction[6:0]), .b(7'b0100011), .eq(S));  // open: gt, lt
  Comparator #(.width(7)) comparator_5 (.a(Instruction[6:0]), .b(7'b1100011), .eq(B));  // open: gt, lt
  Comparator #(.width(7)) comparator_6 (.a(Instruction[6:0]), .b(7'b0010111), .eq(is_auipc));  // open: gt, lt
  Comparator #(.width(7)) comparator_7 (.a(Instruction[6:0]), .b(7'b0110111), .eq(is_lui));  // open: gt, lt
  Comparator #(.width(7)) comparator_8 (.a(Instruction[6:0]), .b(7'b1101111), .eq(is_jal));  // open: gt, lt
  Comparator #(.width(7)) comparator_9 (.a(Instruction[6:0]), .b(7'b1100111), .eq(I3));  // open: gt, lt
  and and_1 (is_add, R, f3_0, f7_00);
  and and_2 (is_mul, R, f3_0, f7_01);
  and and_3 (is_sub, R, f3_0, f7_20);
  and and_4 (is_sll, R, f3_1, f7_00);
  and and_5 (is_mulh, R, f3_1, f7_01);
  and and_6 (is_mulhu, R, f3_3, f7_01);
  and and_7 (is_slt, R, f3_2, f7_00);
  and and_8 (is_xor, R, f3_4, f7_00);
  and and_9 (is_srl, R, f3_5, f7_00);
  and and_10 (is_sra, R, f3_5, f7_20);
  and and_11 (is_or, R, f3_6, f7_00);
  and and_12 (is_and, R, f3_7, f7_00);
  Comparator #(.width(3)) comparator_10 (.a(Instruction[14:12]), .b(3'b000), .eq(f3_0));  // open: gt, lt
  Comparator #(.width(3)) comparator_11 (.a(Instruction[14:12]), .b(3'b001), .eq(f3_1));  // open: gt, lt
  Comparator #(.width(3)) comparator_12 (.a(Instruction[14:12]), .b(3'b010), .eq(f3_2));  // open: gt, lt
  Comparator #(.width(3)) comparator_13 (.a(Instruction[14:12]), .b(3'b011), .eq(f3_3));  // open: gt, lt
  Comparator #(.width(3)) comparator_14 (.a(Instruction[14:12]), .b(3'b100), .eq(f3_4));  // open: gt, lt
  Comparator #(.width(3)) comparator_15 (.a(Instruction[14:12]), .b(3'b101), .eq(f3_5));  // open: gt, lt
  Comparator #(.width(3)) comparator_16 (.a(Instruction[14:12]), .b(3'b110), .eq(f3_6));  // open: gt, lt
  Comparator #(.width(3)) comparator_17 (.a(Instruction[14:12]), .b(3'b111), .eq(f3_7));  // open: gt, lt
  and and_13 (is_lb, I1, f3_0);
  and and_14 (is_lh, I1, f3_1);
  and and_15 (is_lw, I1, f3_2);
  and and_16 (is_addi, I2, f3_0);
  and and_17 (is_slli, I2, f3_1, f7_00);
  and and_18 (is_slti, I2, f3_2);
  and and_19 (is_xori, I2, f3_4);
  and and_20 (is_srli, I2, f3_5, f7_00);
  and and_21 (is_srai, I2, f3_5, f7_20);
  and and_22 (is_ori, I2, f3_6);
  and and_23 (is_andi, I2, f3_7);
  and and_24 (is_jalr, I3, f3_0);
  Comparator #(.width(7)) comparator_18 (.a(Instruction[31:25]), .b({7{1'b0}}), .eq(f7_00));  // open: gt, lt
  Comparator #(.width(7)) comparator_19 (.a(Instruction[31:25]), .b(7'b0000001), .eq(f7_01));  // open: gt, lt
  Comparator #(.width(7)) comparator_20 (.a(Instruction[31:25]), .b(7'b0100000), .eq(f7_20));  // open: gt, lt
  and and_25 (is_sb, S, f3_0);
  and and_26 (is_sh, S, f3_1);
  and and_27 (is_sw, S, f3_2);
  not not_1 (not_1_out, BrEq);
  not not_2 (not_2_out, BrLt);
  not not_3 (not_3_out, BrLt);
  and and_28 (is_beq, B, f3_0);
  and and_29 (is_bne, B, f3_1);
  and and_30 (is_blt, B, f3_4);
  and and_31 (is_bge, B, f3_5);
  and and_32 (is_bltu, B, f3_6);
  and and_33 (is_bgeu, B, f3_7);
  and and_34 (and_34_out, is_beq, BrEq);
  and and_35 (and_35_out, is_bne, not_1_out);
  and and_36 (and_36_out, is_blt, BrLt);
  and and_37 (and_37_out, is_bltu, BrLt);
  and and_38 (and_38_out, is_bge, not_2_out);
  and and_39 (and_39_out, is_bgeu, not_3_out);
  or or_1 (or_1_out, and_34_out, and_35_out, and_36_out, and_37_out);
  or or_2 (or_2_out, and_38_out, and_39_out, is_jal, is_jalr);
  or or_3 (PCSel, or_1_out, or_2_out);

  // Other names for the same wires on the sheet: opcode[6:0] = Instruction[6:0]; funct3[2:0] = Instruction[14:12];
  //   funct7[6:0] = Instruction[31:25]; U1 = is_auipc; J = is_jal; U2 = is_lui

  // Notes on the sheet:
  //   INPUTS to your circuit
  //   Connect ROM Input here ->
  //   contents of rom_1 (hex, n*v repeats v):
  //   1001 1401 1601 1081 1481 1581 1101 1201 1281 1681 1301 1381 41 41 41 1041 10c1 1141 1241 12c1 16c1
  //   1341 13c1 1842 1842 1842 4*1064 1074 1074 1067 17c7 2069 2041
  //   ROM FOR CONTROL LOGIC
  //   DON'T CHANGE THE LOCATIONS OF THE INPUTS AND OUTPUTS!
  //   This is only if you choose to do the ROM option
  //   CONNECT
  //   WIRE
  //   TO
  //   USE
  //   ROM
  //   OUTPUT from your circuit
  //   Reminder: If using ROM, use combinational logic for PCSel
endmodule
